# Fritzing sketch Park-me-v4 (saved by Fritzing 0.9.3b)
circuit board: 8.93358cm x 5.54627cm
breadboards: 1

parts:
  R1 = Resistor [tolerance=±5% resistance=3.3k package=THT]
  C7 = Tantalum Capacitor [capacitance=1μF package="100 mil [THT, tantalum]"]
  C9 = Tantalum Capacitor [capacitance=1μF package="200 mil [THT, tantalum]"]
  R2 = Resistor [tolerance=±5% resistance=3.3k package=THT]
  LCD = female pin header, 2 pins [form="♀ (female)"]
  J2 = female pin header, 2 pins [form="♀ (female)"]
  74HCT125_4 = 74x125 [part_number=74x125 package="DIP (Dual Inline) [THT]"]
  74HCT125_3 = 74x125 [part_number=74x125 package="DIP (Dual Inline) [THT]"]
  74HCT125_2 = 74x125 [part_number=74x125 package="DIP (Dual Inline) [THT]"]
  74HCT125_1 = 74x125 [part_number=74x125 package="DIP (Dual Inline) [THT]"]
  part = 74x125 [part_number=74x125 package="DIP (Dual Inline) [THT]"]
  74HCT125 = 74x125 [part_number=74x125 package="DIP (Dual Inline) [THT]"]
  J16 = female pin header, 1 pin [form="♀ (female)"]
  J17 = female pin header, 1 pin [form="♀ (female)"]
  S3 = female pin header, 1 pin [form="♀ (female)"]
  J19 = female pin header, 1 pin [form="♀ (female)"]
  J20 = female pin header, 1 pin [form="♀ (female)"]
  J24 = female pin header, 1 pin [form="♀ (female)"]
  J25 = female pin header, 1 pin [form="♀ (female)"]
  S5 = female pin header, 1 pin [form="♀ (female)"]
  C10 = Tantalum Capacitor [capacitance=1μF package="200 mil [THT, tantalum]"]
  J31 = female pin header, 1 pin [form="♀ (female)"]
  J32 = female pin header, 1 pin [form="♀ (female)"]
  J33 = female pin header, 1 pin [form="♀ (female)"]
  J34 = female pin header, 1 pin [form="♀ (female)"]
  J35 = female pin header, 1 pin [form="♀ (female)"]
  J36 = female pin header, 1 pin [form="♀ (female)"]
  J38 = female pin header, 1 pin [form="♀ (female)"]
  J39 = female pin header, 1 pin [form="♀ (female)"]
  J40 = female pin header, 1 pin [form="♀ (female)"]
  J41 = female pin header, 1 pin [form="♀ (female)"]
  J42 = female pin header, 1 pin [form="♀ (female)"]
  J43 = female pin header, 1 pin [form="♀ (female)"]
  J44 = female pin header, 1 pin [form="♀ (female)"]
  J45 = female pin header, 1 pin [form="♀ (female)"]
  S6 = female pin header, 1 pin [form="♀ (female)"]
  J46 = female pin header, 1 pin [form="♀ (female)"]
  J49 = female pin header, 1 pin [form="♀ (female)"]  # not connected
  J51 = female pin header, 1 pin [form="♀ (female)"]  # not connected
  U1 = ESP32-38PinWide [part_number=ESP32-38PinWide]
  J53 = female pin header, 1 pin [form="♀ (female)"]
  J48 = female pin header, 1 pin [form="♀ (female)"]  # not connected
  J52 = female pin header, 1 pin [form="♀ (female)"]  # not connected
  J47 = female pin header, 1 pin [form="♀ (female)"]  # not connected
  J50 = female pin header, 1 pin [form="♀ (female)"]  # not connected

nets:
  N1: R1.Pin_0, LCD.pin2, U1.GPIO21
  N2: R1.Pin_1, R2.Pin_1, U1.3.3
  GND: C7.-, C9.-, J2.pin2, 74HCT125_4.C4, 74HCT125_3.C3, 74HCT125_2.C2, 74HCT125_1.C1, part.GND, 74HCT125.connector0, 74HCT125.connector3, 74HCT125.connector6, 74HCT125.connector9, 74HCT125.connector12, J17.pin1, J20.pin1, J24.pin1, C10.-, J39.pin1, J45.pin1, J46.pin1, U1.GND, J53.pin1
  N3: C7.+, U1.EN, U1.GPIO16
  5V: C9.+, J2.pin1, part.VCC, 74HCT125.connector13, J16.pin1, J19.pin1, S5.pin1, C10.+, J43.pin1, U1.VIN
  N4: R2.Pin_0, LCD.pin1, U1.GPIO22
  N5: 74HCT125_3.Y3, 74HCT125.connector7, S3.pin1
  N6: 74HCT125_3.A3, 74HCT125.connector8, U1.GPIO19
  N7: J25.pin1, U1.GPIO4
  N8: J31.pin1, U1.GPIO35
  N9: J32.pin1, U1.GPIO25
  N10: J33.pin1, U1.GPIO34
  N11: J34.pin1, U1.GPIO32
  N12: J35.pin1, U1.GPIO26
  N13: J36.pin1, U1.GPIO33
  N14: J38.pin1, U1.GPIO27
  N15: J40.pin1, U1.GPIO17
  N16: J41.pin1, U1.GPIO13
  N17: J42.pin1, U1.GPIO18
  N18: J44.pin1, U1.GPIO2
  N19: S6.pin1, U1.GPIO5

notes:
  LEDs
  GND
  +
  C7
  +5V
  DHT11
  HC-SR04

custom parts:
  74x125: 74x125 quad tristate buffer active low enable. The 74ahc125 variety is useful as a level translator as the inputs are 5V tolorant when run with a VCC of 3.3V (and will thus take a 5V signal in and provide a 3.3V signal out.) As well this part uses schematic subparts so you can drag each of the 4 gates to a different place in schematic view. Note having many (around 10 or more) subpart parts in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
  74x125: 74x125 quad tristate buffer active low enable. The 74ahc125 variety is useful as a level translator as the inputs are 5V tolorant when run with a VCC of 3.3V (and will thus take a 5V signal in and provide a 3.3V signal out.) As well this part uses schematic subparts so you can drag each of the 4 gates to a different place in schematic view. Note having many (around 10 or more) subpart parts in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
  74x125: 74x125 quad tristate buffer active low enable. The 74ahc125 variety is useful as a level translator as the inputs are 5V tolorant when run with a VCC of 3.3V (and will thus take a 5V signal in and provide a 3.3V signal out.) As well this part uses schematic subparts so you can drag each of the 4 gates to a different place in schematic view. Note having many (around 10 or more) subpart parts in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
  74x125: 74x125 quad tristate buffer active low enable. The 74ahc125 variety is useful as a level translator as the inputs are 5V tolorant when run with a VCC of 3.3V (and will thus take a 5V signal in and provide a 3.3V signal out.) As well this part uses schematic subparts so you can drag each of the 4 gates to a different place in schematic view. Note having many (around 10 or more) subpart parts in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
  74x125: 74x125 quad tristate buffer active low enable. The 74ahc125 variety is useful as a level translator as the inputs are 5V tolorant when run with a VCC of 3.3V (and will thus take a 5V signal in and provide a 3.3V signal out.) As well this part uses schematic subparts so you can drag each of the 4 gates to a different place in schematic view. Note having many (around 10 or more) subpart parts in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
  74x125: 74x125 quad tristate buffer active low enable. The 74ahc125 variety is useful as a level translator as the inputs are 5V tolorant when run with a VCC of 3.3V (and will thus take a 5V signal in and provide a 3.3V signal out.) As well this part uses schematic subparts so you can drag each of the 4 gates to a different place in schematic view. Note having many (around 10 or more) subpart parts in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
  ESP32-38PinWide: Generic 38-Pin ESP32 with wide format (only access to one side of pins on a breadboard) based on Stephen Lilley's HiLetgo ESP-WROOM-32 ESP32 ESP-32S Development Board.
